# Fritzing sketch RFID-Auth (saved by Fritzing 0.9.5d)

parts:
  Part1 = Arduino Leonardo (Rev3b)
  U1 = RFID RC522 SIP - 8 pins [chip_label="RFID RC522" package="SIP (Single Inline) [THT]"]
  LED1 = smd LED [color="Red (633nm)" package="0805 [SMD]"]
  R1 = Resistor [tolerance=±5% resistance=220 package="0603 [SMD]"]

nets:
  3V3: Part1.3V3, U1.VCC
  N1: Part1.GND, LED1.cathode
  N2: Part1.D8/A8, R1.Pin_1
  N3: Part1.D9_PWM/A9, U1.RST
  N4: Part1.D10_PWM/A10, U1.NSS

custom parts:
  RFID RC522 SIP - 8 pins: A SIP stand-in part for RFID RC522 . With 8 pins on a 300 mil single inline package (SIP) footprint.
